// Logisim project 3Final.circ as structural Verilog: 4 circuits, main circuit main
module main (
  input  A,
  input  B,
  input  C,
  output Sum_of_minterms,
  output Product_of_Maxterms
);

  wire n3_input_and_1_out_10, n3_input_and_1_out_11, n3_input_and_1_out_12, n3_input_and_2_out_10,
       n3_input_and_2_out_12, n3_input_or_1_out_10, n3_input_or_1_out_11, n3_input_or_1_out_12,
       n3_input_or_2_out_10, n3_input_or_2_out_11, not_1_out_7, not_1_out_8, not_1_out_10;

  NOT not_1 (
    .in_1(A), .in_2(B), .in_4(C), .out_7(not_1_out_7), .out_8(not_1_out_8), .out_10(not_1_out_10));  // open: in_3, in_5, in_6, out_9, out_11, out_12
  _3_input_And u_3_input_and_1 (
    .in_1(A), .in_2(B), .in_3(not_1_out_10), .in_4(not_1_out_10), .in_5(B), .in_6(not_1_out_7), .in_7(C),
    .in_8(not_1_out_8), .in_9(not_1_out_7), .out_10(n3_input_and_1_out_10), .out_11(n3_input_and_1_out_11),
    .out_12(n3_input_and_1_out_12));
  _3_Input_Or u_3_input_or_1 (
    .in_1(A), .in_2(B), .in_3(C), .in_4(A), .in_5(not_1_out_8), .in_6(not_1_out_10), .in_7(not_1_out_7),
    .in_8(B), .in_9(C), .out_10(n3_input_or_1_out_10), .out_11(n3_input_or_1_out_11),
    .out_12(n3_input_or_1_out_12));
  _3_input_And u_3_input_and_2 (
    .in_1(n3_input_or_2_out_11), .in_2(n3_input_or_2_out_10), .in_3(n3_input_or_2_out_10),
    .in_4(n3_input_and_2_out_10), .in_5(n3_input_and_2_out_12), .in_6(n3_input_and_2_out_12),
    .in_7(n3_input_or_1_out_10), .in_8(n3_input_or_1_out_11), .in_9(n3_input_or_1_out_12),
    .out_10(n3_input_and_2_out_10), .out_11(Product_of_Maxterms), .out_12(n3_input_and_2_out_12));
  _3_Input_Or u_3_input_or_2 (
    .in_1(not_1_out_10), .in_2(not_1_out_8), .in_3(not_1_out_7), .in_4(not_1_out_10), .in_5(B),
    .in_6(not_1_out_7), .in_7(n3_input_and_1_out_11), .in_8(n3_input_and_1_out_12),
    .in_9(n3_input_and_1_out_10), .out_10(n3_input_or_2_out_10), .out_11(n3_input_or_2_out_11),
    .out_12(Sum_of_minterms));
endmodule

module _3_input_And (
  input  in_1,
  input  in_2,
  input  in_3,
  input  in_4,
  input  in_5,
  input  in_6,
  input  in_7,
  input  in_8,
  input  in_9,
  output out_10,
  output out_11,
  output out_12
);

  and and_1 (out_10, in_1, in_2, in_3);
  and and_2 (out_11, in_4, in_5, in_6);
  and and_3 (out_12, in_7, in_8, in_9);
endmodule

module _3_Input_Or (
  input  in_1,
  input  in_2,
  input  in_3,
  input  in_4,
  input  in_5,
  input  in_6,
  input  in_7,
  input  in_8,
  input  in_9,
  output out_10,
  output out_11,
  output out_12
);

  or or_1 (out_10, in_1, in_2, in_3);
  or or_2 (out_11, in_4, in_5, in_6);
  or or_3 (out_12, in_7, in_8, in_9);
endmodule

module NOT (
  input  in_1,
  input  in_2,
  input  in_3,
  input  in_4,
  input  in_5,
  input  in_6,
  output out_7,
  output out_8,
  output out_9,
  output out_10,
  output out_11,
  output out_12
);

  not not_1 (out_7, in_1);
  not not_2 (out_8, in_2);
  not not_3 (out_9, in_3);
  not not_4 (out_10, in_4);
  not not_5 (out_11, in_5);
  not not_6 (out_12, in_6);
endmodule
