// Logisim project 5.2Final.circ as structural Verilog: 2 circuits, main circuit main
module main (
  input  in_1,
  input  in_2,
  input  A1,
  input  A2,
  input  A3,
  input  A4,
  input  B1,
  input  B2,
  input  B3,
  input  B4,
  input  in_11,
  output S1,
  output S2,
  output S3,
  output S4,
  output C_out
);

  wire and_1_out, and_2_out, n4_bit_adder_1_cout, n4_bit_adder_1_s1, n4_bit_adder_1_s2, n4_bit_adder_1_s3,
       n4_bit_adder_1_s4, or_2_out;

  or or_1 (C_out, n4_bit_adder_1_cout, or_2_out);
  _4_bit_Adder u_4_bit_adder_1 (
    .M(in_1), .A1(A1), .B1(B1), .A2(A2), .B2(B2), .A3(A3), .B3(B3), .A4(A4), .B4(B4), .S1(n4_bit_adder_1_s1),
    .S2(n4_bit_adder_1_s2), .S4(n4_bit_adder_1_s4), .Cout(n4_bit_adder_1_cout), .S3(n4_bit_adder_1_s3));
  and and_1 (and_1_out, n4_bit_adder_1_s3, n4_bit_adder_1_s4);
  and and_2 (and_2_out, n4_bit_adder_1_s4, n4_bit_adder_1_s2);
  or or_2 (or_2_out, and_1_out, and_2_out);
  _4_bit_Adder u_4_bit_adder_2 (
    .M(in_2), .A1(n4_bit_adder_1_s1), .B1(in_11), .A2(n4_bit_adder_1_s2), .B2(C_out), .A3(n4_bit_adder_1_s3),
    .B3(C_out), .A4(n4_bit_adder_1_s4), .B4(in_11), .S1(S1), .S2(S2), .S4(S4), .S3(S3));  // open: Cout
endmodule

module _4_bit_Adder (
  input  M,
  input  A1,
  input  B1,
  input  A2,
  input  B2,
  input  A3,
  input  B3,
  input  A4,
  input  B4,
  output S1,
  output S2,
  output S3,
  output S4,
  output Cout
);

  wire adder_1_cout, adder_2_cout, adder_3_cout, xor_1_out, xor_2_out, xor_3_out, xor_4_out;

  xor xor_1 (xor_1_out, B1, M);
  xor xor_2 (xor_2_out, B2, M);
  xor xor_3 (xor_3_out, B3, M);
  xor xor_4 (xor_4_out, B4, M);
  Adder #(.width(1)) adder_1 (.a(A1), .b(xor_1_out), .out(S1), .cin(M), .cout(adder_1_cout));
  Adder #(.width(1)) adder_2 (.a(A2), .b(xor_2_out), .out(S2), .cin(adder_1_cout), .cout(adder_2_cout));
  Adder #(.width(1)) adder_3 (.a(A3), .b(xor_3_out), .out(S3), .cin(adder_2_cout), .cout(adder_3_cout));
  Adder #(.width(1)) adder_4 (.a(A4), .b(xor_4_out), .out(S4), .cin(adder_3_cout), .cout(Cout));
endmodule
