// Logisim project D1.circ as structural Verilog: 7 circuits, main circuit main
module main (
  input  A,
  input  B,
  input  A_2,
  input  B_2,
  input  A_3,
  input  B_3,
  input  A_4,
  input  A_5,
  input  B_4,
  input  A_6,
  input  B_5
);

  wire ic7400_nand_1_out_11, ic7402_nor_1_out_15, ic7404_not_1_out_12, ic7408_and_1_out_12,
       ic7432_or_1_out_12, ic7486_xor_1_out_11;

  LED led_1 (.in(ic7408_and_1_out_12));
  LED led_2 (.in(ic7486_xor_1_out_11));
  IC7486_XOR ic7486_xor_1 (
    .in_5(B_4), .in_6(A_5), .out_11(ic7486_xor_1_out_11));  // open: in_1, in_2, in_3, in_4, in_7, in_8, out_9, out_10, out_12
  IC7408_AND ic7408_and_1 (
    .in_7(B_2), .out_12(ic7408_and_1_out_12), .in_8(A_4));  // open: in_1, in_2, out_9, in_3, out_10, in_4, in_5, out_11, in_6
  LED led_3 (.in(ic7432_or_1_out_12));
  LED led_4 (.in(ic7402_nor_1_out_15));
  IC7400_NAND ic7400_nand_1 (
    .in_5(A_2), .in_6(B_3), .out_11(ic7400_nand_1_out_11));  // open: in_1, in_2, in_3, in_4, in_7, in_8, out_9, out_10, out_12
  LED led_5 (.in(ic7400_nand_1_out_11));
  IC7432_OR ic7432_or_1 (
    .in_7(A), .in_8(B), .out_12(ic7432_or_1_out_12));  // open: in_1, in_2, in_3, in_4, in_5, in_6, out_9, out_10, out_11
  LED led_6 (.in(ic7404_not_1_out_12));
  IC7402_NOR ic7402_nor_1 (
    .in_5(B_5), .in_6(A_6), .out_15(ic7402_nor_1_out_15));  // open: in_1, in_2, in_3, in_4, in_7, in_8, in_9, in_10, in_11, in_12, out_13, out_14, out_16, out_17, out_18
  IC7404_NOT ic7404_not_1 (
    .in_6(A_3), .out_12(ic7404_not_1_out_12));  // open: in_1, in_2, in_3, in_4, in_5, out_7, out_8, out_9, out_10, out_11

  // Notes on the sheet:
  //   F
  //   F
  //   F
  //   F
  //   F
  //   B
endmodule

module IC7408_AND (
  input  in_1,
  input  in_2,
  input  in_3,
  input  in_4,
  input  in_5,
  input  in_6,
  input  in_7,
  input  in_8,
  output out_9,
  output out_10,
  output out_11,
  output out_12
);

  and and_1 (out_9, in_1, in_2);
  and and_2 (out_10, in_3, in_4);
  and and_3 (out_11, in_5, in_6);
  and and_4 (out_12, in_7, in_8);
endmodule

module IC7432_OR (
  input  in_1,
  input  in_2,
  input  in_3,
  input  in_4,
  input  in_5,
  input  in_6,
  input  in_7,
  input  in_8,
  output out_9,
  output out_10,
  output out_11,
  output out_12
);

  or or_1 (out_9, in_1, in_2);
  or or_2 (out_10, in_3, in_4);
  or or_3 (out_11, in_5, in_6);
  or or_4 (out_12, in_7, in_8);
endmodule

module IC7400_NAND (
  input  in_1,
  input  in_2,
  input  in_3,
  input  in_4,
  input  in_5,
  input  in_6,
  input  in_7,
  input  in_8,
  output out_9,
  output out_10,
  output out_11,
  output out_12
);

  nand nand_1 (out_9, in_1, in_2);
  nand nand_2 (out_10, in_3, in_4);
  nand nand_3 (out_11, in_5, in_6);
  nand nand_4 (out_12, in_7, in_8);
endmodule

module IC7486_XOR (
  input  in_1,
  input  in_2,
  input  in_3,
  input  in_4,
  input  in_5,
  input  in_6,
  input  in_7,
  input  in_8,
  output out_9,
  output out_10,
  output out_11,
  output out_12
);

  xor xor_1 (out_9, in_1, in_2);
  xor xor_2 (out_10, in_3, in_4);
  xor xor_3 (out_11, in_5, in_6);
  xor xor_4 (out_12, in_7, in_8);
endmodule

module IC7404_NOT (
  input  in_1,
  input  in_2,
  input  in_3,
  input  in_4,
  input  in_5,
  input  in_6,
  output out_7,
  output out_8,
  output out_9,
  output out_10,
  output out_11,
  output out_12
);

  not not_1 (out_7, in_1);
  not not_2 (out_8, in_2);
  not not_3 (out_9, in_3);
  not not_4 (out_10, in_4);
  not not_5 (out_11, in_5);
  not not_6 (out_12, in_6);
endmodule

module IC7402_NOR (
  input  in_1,
  input  in_2,
  input  in_3,
  input  in_4,
  input  in_5,
  input  in_6,
  input  in_7,
  input  in_8,
  input  in_9,
  input  in_10,
  input  in_11,
  input  in_12,
  output out_13,
  output out_14,
  output out_15,
  output out_16,
  output out_17,
  output out_18
);

  nor nor_1 (out_13, in_1, in_2);
  nor nor_2 (out_14, in_3, in_4);
  nor nor_3 (out_15, in_5, in_6);
  nor nor_4 (out_16, in_7, in_8);
  nor nor_5 (out_17, in_9, in_10);
  nor nor_6 (out_18, in_11, in_12);
endmodule
