// Logisim project Lab8.2.circ as structural Verilog: 1 circuit, main circuit main
module main (
  input  X,
  output Y
);

  wire and_1_out, and_2_out, clock_1_out, not_1_out, or_1_out, t_ff_1_q, t_ff_1_qn, t_ff_2_q, t_ff_2_qn;

  not not_1 (not_1_out, X);
  and and_1 (and_1_out, t_ff_2_q, X, t_ff_1_qn);
  and and_2 (and_2_out, t_ff_1_qn, not_1_out, t_ff_2_qn);
  or or_1 (or_1_out, and_1_out, and_2_out);
  Clock clock_1 (.out(clock_1_out));
  T_Flip_Flop t_ff_1 (.clk(clock_1_out), .T(X), .Q(t_ff_1_q), .Qn(t_ff_1_qn));  // open: preset, reset, en
  T_Flip_Flop t_ff_2 (.clk(clock_1_out), .T(or_1_out), .Q(t_ff_2_q), .Qn(t_ff_2_qn));  // open: preset, reset, en
  and and_3 (Y, X, t_ff_1_qn);
endmodule
