// Logisim project Lab8.3.circ as structural Verilog: 1 circuit, main circuit main
module main (
  input  X,
  output Y
);

  wire and_1_out, clock_1_out, j_k_ff_1_q, j_k_ff_1_qn, not_1_out;

  not not_1 (not_1_out, X);
  and and_1 (and_1_out, j_k_ff_1_qn, not_1_out);
  Clock clock_1 (.out(clock_1_out));
  J_K_Flip_Flop j_k_ff_1 (
    .J(X), .clk(clock_1_out), .K(X), .Q(j_k_ff_1_q), .Qn(j_k_ff_1_qn));  // open: preset, en, reset
  J_K_Flip_Flop j_k_ff_2 (.J(and_1_out), .clk(clock_1_out), .K(X));  // open: Q, Qn, preset, en, reset
  and and_2 (Y, j_k_ff_1_qn, X);
endmodule
