// Logisim project Lab@2A.circ as structural Verilog: 4 circuits, main circuit main
module main (
  input  A,
  input  B,
  input  A_2,
  input  B_2
);

  wire xnor_1_out_3, XOR_out_3;

  XOR XOR (.in_1(A), .in_2(B), .out_3(XOR_out_3));
  LED led_1 (.in(XOR_out_3));
  XNOR xnor_1 (.out_3(xnor_1_out_3), .in_1(A_2), .in_2(B_2));
  LED led_2 (.in(xnor_1_out_3));

  // Notes on the sheet:
  //   XNOR
  //   F
  //   F
endmodule

module NAND_IC7400 (
  input  in_1,
  input  in_2,
  input  in_3,
  input  in_4,
  input  in_5,
  input  in_6,
  input  in_7,
  input  in_8,
  output out_9,
  output out_10,
  output out_11,
  output out_12
);

  nand nand_1 (out_9, in_1, in_2);
  nand nand_2 (out_10, in_3, in_4);
  nand nand_3 (out_11, in_5, in_6);
  nand nand_4 (out_12, in_7, in_8);
endmodule

module XOR (
  input  in_1,
  input  in_2,
  output out_3
);

  wire nand_ic7400_1_out_10, nand_ic7400_2_out_9, nand_ic7400_3_out_10;

  NAND_IC7400 nand_ic7400_1 (
    .in_3(in_1), .in_4(in_2), .out_10(nand_ic7400_1_out_10));  // open: in_1, in_2, in_5, in_6, in_7, in_8, out_9, out_11, out_12
  NAND_IC7400 nand_ic7400_2 (
    .in_1(in_1), .in_2(nand_ic7400_1_out_10), .out_9(nand_ic7400_2_out_9));  // open: in_3, in_4, in_5, in_6, in_7, in_8, out_10, out_11, out_12
  NAND_IC7400 nand_ic7400_3 (
    .in_3(nand_ic7400_1_out_10), .in_4(in_2), .out_10(nand_ic7400_3_out_10));  // open: in_1, in_2, in_5, in_6, in_7, in_8, out_9, out_11, out_12
  NAND_IC7400 nand_ic7400_4 (
    .in_1(nand_ic7400_2_out_9), .in_2(nand_ic7400_3_out_10), .out_9(out_3));  // open: in_3, in_4, in_5, in_6, in_7, in_8, out_10, out_11, out_12
endmodule

module XNOR (
  input  in_1,
  input  in_2,
  output out_3
);

  wire nand_ic7400_1_out_10, nand_ic7400_2_out_10, nand_ic7400_3_out_9, nand_ic7400_4_out_9;

  NAND_IC7400 nand_ic7400_1 (
    .in_3(in_1), .in_4(in_2), .out_10(nand_ic7400_1_out_10));  // open: in_1, in_2, in_5, in_6, in_7, in_8, out_9, out_11, out_12
  NAND_IC7400 nand_ic7400_2 (
    .in_3(nand_ic7400_1_out_10), .in_4(in_2), .out_10(nand_ic7400_2_out_10));  // open: in_1, in_2, in_5, in_6, in_7, in_8, out_9, out_11, out_12
  NAND_IC7400 nand_ic7400_3 (
    .in_1(in_1), .in_2(nand_ic7400_1_out_10), .out_9(nand_ic7400_3_out_9));  // open: in_3, in_4, in_5, in_6, in_7, in_8, out_10, out_11, out_12
  NAND_IC7400 nand_ic7400_4 (
    .in_1(nand_ic7400_3_out_9), .in_2(nand_ic7400_2_out_10), .out_9(nand_ic7400_4_out_9));  // open: in_3, in_4, in_5, in_6, in_7, in_8, out_10, out_11, out_12
  NAND_IC7400 nand_ic7400_5 (
    .in_1(nand_ic7400_4_out_9), .in_2(nand_ic7400_4_out_9), .out_9(out_3));  // open: in_3, in_4, in_5, in_6, in_7, in_8, out_10, out_11, out_12
endmodule
