// Logisim project MuxLab6.circ as structural Verilog: 1 circuit, main circuit main
module main (
  input  D,
  input  in_2,
  input  D_Enabler,
  input  [2:0] in_4,
  output out_5
);

  Multiplexer #(.select(3)) multiplexer_1 (
    .in0(1'b1), .in1(D), .in2(D), .in3(in_2), .in4(1'b1), .in5(in_2), .in6(in_2), .in7(1'b1), .out(out_5),
    .sel(in_4), .en(D_Enabler));
endmodule
