// Logisim project lab 7 decoder.circ as structural Verilog: 1 circuit, main circuit main
module main (
  input  A,
  input  B,
  input  C,
  input  D
);

  wire and_1_out, and_2_out, and_3_out, and_4_out, and_5_out, and_6_out, and_7_out, and_8_out, and_9_out,
       and_10_out, and_11_out, and_12_out, nand_1_out, nand_2_out, nand_3_out, nand_4_out, nand_5_out,
       nand_6_out, nand_7_out, nand_8_out, nand_9_out, nand_10_out, nand_11_out, nand_12_out, nand_13_out,
       nand_14_out, nand_15_out, nand_16_out, nand_17_out, nand_18_out, nand_19_out, nand_20_out,
       nand_21_out, nand_22_out, nand_23_out, nand_24_out, nand_25_out, nand_26_out, nand_27_out,
       nand_28_out, nand_29_out, nand_30_out, nand_31_out, nand_32_out, nand_33_out, nand_34_out,
       nand_35_out, nand_36_out, nand_37_out, nand_38_out, nand_39_out, nand_40_out, nand_41_out,
       nand_42_out, nand_43_out, nand_44_out, nand_45_out, nand_46_out, nand_47_out, nand_48_out, nand_49_out;

  nand nand_1 (nand_1_out, B, B);
  nand nand_2 (nand_2_out, D, D);
  nand nand_3 (nand_3_out, C, C);
  nand nand_4 (nand_4_out, D, D);
  nand nand_5 (nand_5_out, D, D);
  nand nand_6 (nand_6_out, B, B);
  nand nand_7 (nand_7_out, D, D);
  nand nand_8 (nand_8_out, B, B);
  nand nand_9 (nand_9_out, C, C);
  nand nand_10 (nand_10_out, B, B);
  nand nand_11 (nand_11_out, D, D);
  nand nand_12 (nand_12_out, D, D);
  nand nand_13 (nand_13_out, C, C);
  nand nand_14 (nand_14_out, D, D);
  nand nand_15 (nand_15_out, C, C);
  nand nand_16 (nand_16_out, D, D);
  nand nand_17 (nand_17_out, B, B);
  nand nand_18 (nand_18_out, C, C);
  nand nand_19 (nand_19_out, D, D);
  nand nand_20 (nand_20_out, nand_1_out, nand_2_out);
  nand nand_21 (nand_21_out, C, C);
  nand nand_22 (nand_22_out, B, D);
  nand nand_23 (nand_23_out, A, A);
  nand nand_24 (nand_24_out, nand_3_out, nand_4_out);
  and and_1 (and_1_out, C, nand_5_out);
  nand nand_25 (nand_25_out, B, B);
  nand nand_26 (nand_26_out, nand_6_out, nand_7_out);
  nand nand_27 (nand_27_out, nand_8_out, C);
  nand nand_28 (nand_28_out, D, D);
  and and_2 (and_2_out, B, nand_9_out);
  nand nand_29 (nand_29_out, nand_10_out, nand_11_out);
  nand nand_30 (nand_30_out, C, nand_12_out);
  nand nand_31 (nand_31_out, nand_13_out, nand_14_out);
  nand nand_32 (nand_32_out, B, nand_15_out);
  nand nand_33 (nand_33_out, B, nand_16_out);
  nand nand_34 (nand_34_out, A, A);
  nand nand_35 (nand_35_out, nand_17_out, C);
  nand nand_36 (nand_36_out, B, nand_18_out);
  nand nand_37 (nand_37_out, C, nand_19_out);
  nand nand_38 (nand_38_out, A, A);
  and and_3 (and_3_out, nand_20_out, nand_21_out);
  and and_4 (and_4_out, nand_22_out, nand_23_out);
  and and_5 (and_5_out, B, nand_24_out);
  nand nand_39 (nand_39_out, C, D);
  nand nand_40 (nand_40_out, and_1_out, nand_25_out);
  and and_6 (and_6_out, nand_26_out, nand_27_out);
  nand nand_41 (nand_41_out, C, nand_28_out);
  nand nand_42 (nand_42_out, and_2_out, D);
  nand nand_43 (nand_43_out, A, A);
  nand nand_44 (nand_44_out, nand_29_out, nand_30_out);
  and and_7 (and_7_out, nand_31_out, nand_32_out);
  and and_8 (and_8_out, nand_33_out, nand_34_out);
  and and_9 (and_9_out, nand_35_out, nand_36_out);
  and and_10 (and_10_out, nand_37_out, nand_38_out);
  nand nand_45 (nand_45_out, and_3_out, and_4_out);
  nand nand_46 (nand_46_out, and_5_out, nand_39_out);
  and and_11 (and_11_out, and_6_out, nand_41_out);
  and and_12 (and_12_out, nand_42_out, nand_43_out);
  nand nand_47 (nand_47_out, and_7_out, and_8_out);
  nand nand_48 (nand_48_out, and_9_out, and_10_out);
  nand nand_49 (nand_49_out, and_11_out, and_12_out);
  _7_Segment_Display u_7_segment_display_1 (
    .g(nand_48_out), .f(nand_47_out), .a(nand_45_out), .b(nand_46_out), .e(nand_44_out), .d(nand_49_out),
    .c(nand_40_out));  // open: dp
endmodule
